# Fritzing sketch Bomb (saved by Fritzing 0.9.3b)

parts:
  WeMos_D1_Mini1 = WeMos D1 Mini
  Part1 = TM1637 4-Digit 7-Segment Display
  U1 = MIDI_CONN_FEMALE [package=din_5_female]  # not connected
  Part2 = Arduino Uno (Rev3)  # not connected
  J1 = female pin header, 1 pin [form="♀ (female)"]
  J2 = female pin header, 1 pin [form="♀ (female)"]

nets:
  5V: WeMos_D1_Mini1.5V, Part1.VCC
  N1: WeMos_D1_Mini1.D2, Part1.CLK
  N2: WeMos_D1_Mini1.D3, Part1.DIO
  N3: WeMos_D1_Mini1.G, Part1.GND
  N4: J1.pin1, J2.pin1

custom parts:
  WeMos D1 Mini: The D1 mini is a mini wifi board based on ESP-8266EX.
  TM1637 4-Digit 7-Segment Display: A 4-digit 7-segment display based on the TM1637 chipset
